// Digital circuit add_4bits.dig as structural Verilog
module add_4bits (
  input  A0,
  input  B0,
  input  A1,
  input  B1,
  input  A2,
  input  B2,
  input  A3,
  input  B3,
  input  C0,
  output Ci_plus_1,
  output Z0,
  output Z1,
  output Z2,
  output Z3
);

  wire composantstp_1_p5, composantstp_2_p5, composantstp_3_p5;

  // ComposantsTP composantstp_1: pin names not known; wires that end beside it: C0, B0, A0, Z0, composantstp_1_p5
  // ComposantsTP composantstp_2: pin names not known; wires that end beside it: composantstp_1_p5, B1, A1, Z1, composantstp_2_p5
  // ComposantsTP composantstp_3: pin names not known; wires that end beside it: composantstp_2_p5, B2, A2, Z2, composantstp_3_p5
  // ComposantsTP composantstp_4: pin names not known; wires that end beside it: composantstp_3_p5, B3, A3, Z3, Ci_plus_1
  LED led_1 (.in(Ci_plus_1));
endmodule

/* Test case Ci+1:
A0 A1 A2 A3 B0 B1 B2 B3 C0 Z0 Z1 Z2 Z3 Ci+1
1 1 1 1 1 1 1 1 0 0 1 1 1 1  
0 0 0 0 0 0 0 0 0 0 0 0 0 0
1 0 1 0 0 1 0 1 0 1 1 1 1 0
0 1 1 1 1 0 1 1 1 0 0 1 1 1
1 1 1 1 0 0 1 0 0 1 1 0 0 1
1 0 0 0 1 0 0 0 1 1 1 0 0 0
*/
